# Fritzing sketch pico_diagram (saved by Fritzing 0.9.3b)
breadboards: 1

parts:
  Mod1 = Raspberry Pi Pico
  IC1 = 25LC512 [package=THT]
  IC2 = 25LC512 [package=THT]
  LED1 = smd LED [color="Green (555nm)" package="0805 [SMD]"]
  LED2 = smd LED [color="Blue (430nm)" package="0805 [SMD]"]  # not connected
  LED3 = smd LED [color="Red (633nm)" package="0805 [SMD]"]
  Grove1 = Grove OLED 128x96
  RE1 = Rotary Encoder [package=THT]
  R1 = Resistor [tolerance=±5% resistance=3.3k package=THT]
  R2 = Resistor [tolerance=±5% resistance=3.3k package=THT]
  R3 = Resistor [tolerance=±5% resistance=3.3k package=THT]
  S1 = Pushbutton [package="[THT]"]

nets:
  N1: Mod1.pin_3, Mod1.pin_8, Mod1.pin_13, Mod1.pin_18, Mod1.pin_23, Mod1.pin_28, Mod1.pin_33, Mod1.pin_38, IC1.0V, IC2.0V, LED1.anode, LED3.anode, Grove1.GND, S1.Pin_1, S1.Pin_2
  N2: Mod1.pin_6, Grove1.SDA
  N3: Mod1.pin_7, Grove1.SCL
  N4: Mod1.pin_10, RE1.EncoderPinB
  N5: Mod1.pin_11, RE1.EncoderPinC
  N6: Mod1.pin_12, RE1.EncoderPinA
  N7: Mod1.pin_15, R2.Pin_0
  N8: Mod1.pin_16, R1.Pin_0
  N9: Mod1.pin_17, R3.Pin_0
  N10: Mod1.pin_21, IC1.SO_-_Data_Out, IC2.SO_-_Data_Out
  N11: Mod1.pin_24, IC1.SCK_-_SPI_Clock, IC2.SCK_-_SPI_Clock
  N12: Mod1.pin_25, IC1.SI_-_Data_In, IC2.SI_-_Data_In
  N13: Mod1.pin_26, IC1.CS_-_Chip_Select
  N14: Mod1.pin_29, IC2.CS_-_Chip_Select
  N15: Mod1.pin_36, IC1.HOLD, IC1.+V, IC2.HOLD, IC2.+V
  N16: Mod1.pin_37, S1.Pin_3, S1.Pin_4
  N17: IC1.WP_-_Write_Protect, IC2.WP_-_Write_Protect, Grove1.VCC
  N18: LED1.cathode, R2.Pin_1
  N19: LED3.cathode, R1.Pin_1

custom parts:
  Raspberry Pi Pico: Raspberry Pi Pico. Based around the RP2040 microcontroller the Pico is a low cost microcontroller device bringing Raspberry Pi quality, cost, and easy of use to the microcontroller space. Jan 2021, Split part in to two versions: tht (this one) and SMD. This one will drill holes for a .1 in header in pcb to allow plugging in the module as well as providing pads to solder the module to the top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
